// Logisim project Act_2.circ as structural Verilog: 6 circuits, main circuit main
module main (
  input  [1:0] in_1,
  input  in_2,
  input  in_3,
  input  in_4,
  input  in_5
);

  wire selector_leds_1_comparador, selector_leds_1_decimal_a, selector_leds_1_decimal_b,
       selector_leds_1_sumador;
  wire [6:0] comparador_2bits_1_s0, decodificador_7seg_a0_1_s0, decodificador_7seg_a1_1_s0,
       multiplexer_1_out, sumador_2bits_1_s0;

  Decodificador_7seg_A0 decodificador_7seg_a0_1 (.A1(in_4), .A0(in_5), .S0(decodificador_7seg_a0_1_s0));
  Decodificador_7seg_A1 decodificador_7seg_a1_1 (.B1(in_2), .B2(in_3), .S0(decodificador_7seg_a1_1_s0));
  Sumador_2bits sumador_2bits_1 (.A1(in_4), .A0(in_5), .B1(in_2), .B0(in_3), .S0(sumador_2bits_1_s0));
  Comparador_2bits comparador_2bits_1 (.A1(in_4), .A0(in_5), .B1(in_2), .B0(in_3), .S0(comparador_2bits_1_s0));
  Multiplexer #(.select(2), .width(7)) multiplexer_1 (
    .in0(decodificador_7seg_a0_1_s0), .in1(decodificador_7seg_a1_1_s0), .in2(sumador_2bits_1_s0),
    .in3(comparador_2bits_1_s0), .out(multiplexer_1_out), .sel(in_1));
  _7_Segment_Display u_7_segment_display_1 (
    .g(multiplexer_1_out[0]), .f(multiplexer_1_out[1]), .a(multiplexer_1_out[6]), .b(multiplexer_1_out[5]),
    .e(multiplexer_1_out[2]), .d(multiplexer_1_out[3]), .c(multiplexer_1_out[4]));  // open: dp
  LED led_1 (.in(selector_leds_1_decimal_a));
  Selector_leds selector_leds_1 (
    .E0({in_2, in_3}), .Decimal_A(selector_leds_1_decimal_a), .Decimal_B(selector_leds_1_decimal_b),
    .Comparador(selector_leds_1_comparador), .Sumador(selector_leds_1_sumador));
  LED led_2 (.in(selector_leds_1_decimal_b));
  LED led_3 (.in(selector_leds_1_comparador));
  LED led_4 (.in(selector_leds_1_sumador));

  // Notes on the sheet:
  //   A1 A0
  //   B0 B1
endmodule

module Decodificador_7seg_A0 (
  input  A1,
  input  A0,
  output [6:0] S0
);

  wire not_1_out;

  not not_1 (not_1_out, A1);
  not not_2 (S0[2], A0);
  or or_1 (S0[6], S0[2], A1);
  or or_2 (S0[4], not_1_out, A0);
  or or_3 (S0[3], S0[2], A1);
  and and_1 (S0[1], not_1_out, S0[2]);

  assign {S0[5], S0[0]} = {1'b1, A1};
endmodule

module Decodificador_7seg_A1 (
  input  B1,
  input  B2,
  output [6:0] S0
);

  wire not_1_out;

  not not_1 (not_1_out, B1);
  not not_2 (S0[2], B2);
  or or_1 (S0[6], S0[2], B1);
  or or_2 (S0[4], not_1_out, B2);
  or or_3 (S0[3], S0[2], B1);
  and and_1 (S0[1], not_1_out, S0[2]);

  assign {S0[5], S0[0]} = {1'b1, B1};
endmodule

module Sumador_2bits (
  input  A1,
  input  A0,
  input  B1,
  input  B0,
  output [6:0] S0
);

  wire and_1_out, and_2_out, and_3_out, and_4_out, and_5_out, and_6_out, and_7_out, and_8_out, and_9_out,
       and_10_out, and_11_out, and_12_out, and_13_out, and_14_out, and_15_out, and_16_out, and_17_out,
       and_18_out, and_19_out, and_20_out, and_21_out, and_22_out, and_23_out, and_24_out, and_25_out,
       and_26_out, and_27_out, and_28_out, and_29_out, not_1_out, not_2_out, not_3_out, not_4_out;

  not not_1 (not_1_out, A1);
  not not_2 (not_2_out, A0);
  not not_3 (not_3_out, B1);
  not not_4 (not_4_out, B0);
  and and_1 (and_1_out, not_1_out, A0, not_3_out, B0);
  and and_2 (and_2_out, not_1_out, not_2_out, not_4_out);
  and and_3 (and_3_out, not_1_out, not_2_out, B1);
  and and_4 (and_4_out, not_1_out, B1, not_4_out);
  and and_5 (and_5_out, A1, not_2_out, B0);
  and and_6 (and_6_out, A1, not_3_out, not_4_out);
  and and_7 (and_7_out, A1, A0, B1);
  and and_8 (and_8_out, not_2_out, not_4_out);
  and and_9 (and_9_out, A1, B1);
  and and_10 (and_10_out, not_1_out, not_3_out, not_4_out);
  and and_11 (and_11_out, not_2_out, B0);
  and and_12 (and_12_out, A0, B1);
  and and_13 (and_13_out, A1, A0);
  and and_14 (and_14_out, not_1_out, A0, not_3_out, B0);
  and and_15 (and_15_out, not_1_out, not_2_out, not_4_out);
  and and_16 (and_16_out, not_1_out, not_2_out, B1);
  and and_17 (and_17_out, not_1_out, B1, not_4_out);
  and and_18 (and_18_out, A1, not_2_out, B0);
  and and_19 (and_19_out, A1, not_3_out, not_4_out);
  and and_20 (and_20_out, A1, A0, B1);
  and and_21 (and_21_out, not_1_out, not_2_out, not_4_out);
  and and_22 (and_22_out, not_1_out, A0, not_3_out, B0);
  and and_23 (and_23_out, not_2_out, not_3_out, not_4_out);
  and and_24 (and_24_out, A1, A0, B1, B0);
  and and_25 (and_25_out, not_1_out, not_2_out, not_3_out, not_4_out);
  and and_26 (and_26_out, A0, B1, B0);
  and and_27 (and_27_out, A1, B1);
  and and_28 (and_28_out, A1, A0, B0);
  and and_29 (and_29_out, A0, B0);
  or or_1 (S0[6], and_1_out, and_2_out, and_3_out, and_4_out, and_5_out, and_6_out, and_7_out);
  or or_2 (S0[5], not_1_out, not_3_out, and_8_out);
  or or_3 (S0[4], and_9_out, and_10_out, and_11_out, and_12_out, and_13_out);
  or or_4 (S0[3], and_14_out, and_15_out, and_16_out, and_17_out, and_18_out, and_19_out, and_20_out);
  or or_5 (S0[2], and_21_out, and_22_out, and_23_out, and_24_out);
  or or_6 (S0[1], and_25_out, and_26_out, and_27_out, and_28_out);
  or or_7 (S0[0], B1, and_29_out, A1);
endmodule

module Comparador_2bits (
  input  A1,
  input  A0,
  input  B1,
  input  B0,
  output [6:0] S0
);

  wire and_1_out, and_2_out, and_3_out, and_4_out, and_5_out, and_6_out, and_7_out, and_8_out, and_9_out,
       and_10_out, and_11_out, and_12_out, and_13_out, not_1_out, not_2_out;

  not not_1 (not_1_out, B1);
  not not_2 (not_2_out, B0);
  and and_1 (and_1_out, not_1_out, not_2_out);
  and and_2 (and_2_out, A0, not_1_out);
  and and_3 (and_3_out, A1, not_1_out);
  and and_4 (and_4_out, A1, not_2_out);
  and and_5 (and_5_out, A1, A0);
  and and_6 (and_6_out, A0, not_1_out, not_2_out);
  and and_7 (and_7_out, A1, not_1_out);
  and and_8 (and_8_out, A1, A0, not_2_out);
  and and_9 (and_9_out, not_1_out, not_2_out);
  and and_10 (and_10_out, A0, not_1_out);
  and and_11 (and_11_out, A1, not_1_out);
  and and_12 (and_12_out, A1, not_2_out);
  and and_13 (and_13_out, A1, A0);
  or or_1 (S0[6], and_1_out, and_2_out, and_3_out, and_4_out, and_5_out);
  or or_2 (S0[4], and_6_out, and_7_out, and_8_out);
  or or_3 (S0[0], and_9_out, and_10_out, and_11_out, and_12_out, and_13_out);

  assign {S0[5], S0[3:1]} = 4'b0111;
endmodule

module Selector_leds (
  input  [1:0] E0,
  output Decimal_A,
  output Decimal_B,
  output Comparador,
  output Sumador
);

  wire nand_1_out, nand_2_out, nand_3_out, nand_4_out, nand_5_out, nand_6_out;

  nand nand_1 (nand_1_out, 1'b1, E0[1]);
  nand nand_2 (nand_2_out, 1'b1, E0[0]);
  nand nand_3 (nand_3_out, nand_1_out, nand_2_out);
  nand nand_4 (nand_4_out, nand_1_out, E0[0]);
  nand nand_5 (nand_5_out, E0[1], nand_2_out);
  nand nand_6 (nand_6_out, E0[1], E0[0]);
  nand nand_7 (Decimal_A, nand_3_out, nand_3_out);
  nand nand_8 (Decimal_B, nand_4_out, nand_4_out);
  nand nand_9 (Comparador, nand_5_out, nand_5_out);
  nand nand_10 (Sumador, nand_6_out, nand_6_out);
endmodule
